# Fritzing sketch TSE (saved by Fritzing 0.9.9b)
circuit board: 9.34654cm x 6.53135cm
breadboards: 1

parts:
  M1 = BluePill
  U1 = MCP2551 [package=so08]
  JP1 = Header 6 [package=molex-1x6_lock]
  JP2 = Header 6 [package=molex-1x6_lock]
  R1 = Resistor [tolerance=±5% resistance=2.20 package=THT]
  C1 = Electrolytic Capacitor [capacitance=10µF voltage=35V package="100 mil [THT, electrolytic]"]
  Cadende = Rotary Potentiometer (Small) [maximum_resistance=25kΩ package=THT]
  Torque = Rotary Potentiometer (Small) [maximum_resistance=25kΩ package=THT]
  S1 = Pushbutton [package="[THT]"]
  S2 = SPST Switch [package=switch-spst-smd-a]

nets:
  N1: M1.A0, S1.Pin_1, S1.Pin_2
  N2: M1.A1, Cadende.wiper
  N3: M1.A2, Torque.wiper
  N4: M1.A3, JP1.2
  N5: M1.A4, S2.S
  N6: M1.3V3, Cadende.leg2, Torque.leg2
  GND: M1.GND, U1.VSS, JP1.6, JP2.6, S1.Pin_3, S1.Pin_4
  N7: M1.A8, R1.Pin_0
  N8: M1.A9, JP1.3, JP2.3
  N9: M1.A10, JP1.4, JP2.4
  N10: M1.A11, U1.RXD
  N11: M1.A12, U1.TXD
  5V: M1.5V, JP1.5, JP2.5
  N12: U1.CANL, JP2.2
  N13: U1.CANH, JP2.1
  N14: JP1.1, R1.Pin_1, C1.+
  N15: C1.-, Cadende.leg1, Torque.leg1, S2.P

notes:
  CAN-H
  CAN-L
  PAS_2
  PAS_1
  +5V
  GND
  torque
  speed/dir

custom parts:
  BluePill: Generic ebay blue pill STM32F103C8 "Blue pill" CPU module. Arm Cortex M3 128KB flash (usually) 20kb ram, RTC on board. Supported by the Arduino IDE for programming. As cheap as an Arduino nano but with more power and memory.
